# Fritzing sketch circuit_design_fritzing (saved by Fritzing 0.9.3b)
breadboards: 1

parts:
  Part1 = Arduino Uno (Rev3)
  S1 = PH meter [package=THT]
  T1 = TMP36 Temperature Sensor [package="TO92 [THT]"]
  부품3 = FC-28 Soil Hygrometer Module
  부품4 = FC-28 Soil Hygrometer Module - Probe
  VCC1 = Battery
  VCC2 = Battery  # not connected
  VCC4 = Battery  # not connected
  VCC3 = Battery

nets:
  N1: Part1.A0, 부품3.AO
  N2: Part1.A1, T1.GND
  N3: Part1.A5/SCL, S1.pin2
  N4: Part1.GND, VCC1.-
  N5: Part1.5V, S1.pin1, T1.+Vs
  N6: Part1.VIN, S1.pin3, T1.Vout, VCC3.+
  N7: 부품3.POS, 부품4.POS
  N8: 부품3.NEG, 부품4.NEG

custom parts:
  FC-28 Soil Hygrometer Module: The FC-28 is a soil hygrometer module that uses the Texas Instruments LM393 comparator chip to provide an analog measurement of soil humidity. The digital output is high when soil moisture is over a certain threshold, as determined by adjusting the potentiometer.
  FC-28 Soil Hygrometer Module - Probe: The FC-28 is a soil hygrometer module that uses the Texas Instruments LM393 comparator chip to provide an analog measurement of soil humidity.
